# Fritzing sketch sketch2 (saved by Fritzing 0.6.3b)
breadboards: 1

parts:
  Arduino1 = Arduino
  LED1 = LED - 5mm [color="Red (633nm)" package="5 mm [THT]"]
  R1 = Resistor [tolerance=±5% resistance=220 package=THT]
  S1 = Pushbutton [package="[THT]"]
  R2 = Resistor [tolerance=±5% resistance=10k package=THT]

nets:
  N1: Arduino1.GND, LED1.cathode, S1.Pin_1, S1.Pin_2
  N2: Arduino1.D9, R1.Pin_1
  N3: Arduino1.D7, S1.Pin_3, S1.Pin_4, R2.Pin_1
  N4: Arduino1.+5V, R2.Pin_0
  N5: LED1.anode, R1.Pin_0
