# Fritzing sketch sketch3 (saved by Fritzing 0.6.3b)
breadboards: 1

parts:
  RGB_Shield = Arduino
  R1 = Resistor [resistance=220 tolerance=±5% package=THT]
  R3 = Resistor [resistance=220 tolerance=±5% package=THT]
  R2 = Resistor [resistance=220 tolerance=±5% package=THT]
  LED1 = RGB LED - (4 legs) [package="5 mm [THT]"]

nets:
  N1: RGB_Shield.D11, R1.Pin_0
  N2: RGB_Shield.D10, R2.Pin_0
  N3: RGB_Shield.D9, R3.Pin_0
  N4: R1.Pin_1, LED1.red_cathode
  N5: R3.Pin_1, LED1.blue_cathode
  N6: R2.Pin_1, LED1.green_cathode
