# Fritzing sketch sketch4 (saved by Fritzing 0.6.3b)
breadboards: 1

parts:
  Arduino1 = Arduino
  LED1 = LED - 5mm [color="Red (633nm)" package="5 mm [THT]"]
  R1 = Resistor [tolerance=±5% resistance=220 package=THT]
  R2 = Rotary Potentiometer (Small) [maximum_resistance=100kΩ]

nets:
  N1: Arduino1.GND, LED1.cathode, R2.leg2
  N2: Arduino1.D9, R1.Pin_1
  N3: Arduino1.+5V, R2.leg1
  N4: Arduino1.A0, R2.wiper
  N5: LED1.anode, R1.Pin_0
