# Fritzing sketch sketch6 (saved by Fritzing 0.6.3b)
breadboards: 1

parts:
  Arduino1 = Arduino
  R1 = Resistor [tolerance=±5% resistance=100 package=THT]
  R2 = Photocell (LDR) [package=THT]
  R3 = Resistor [tolerance=±5% resistance=10k package=THT]
  J1 = Piezo Speaker

nets:
  N1: Arduino1.GND, R3.Pin_0, J1.pin1
  N2: Arduino1.D8, R1.Pin_1
  N3: Arduino1.+5V, R2.pin_1
  N4: Arduino1.A0, R2.pin_0, R3.Pin_1
  N5: R1.Pin_0, J1.pin2
